# Fritzing sketch simon_d1_mini_v4 (saved by Fritzing 0.9.9b)
breadboards: 1

parts:
  WeMos_D1_Mini1 = WeMos D1 Mini
  S1 = Pushbutton [package="[THT]"]
  S2 = Pushbutton [package="[THT]"]
  S3 = Pushbutton [package="[THT]"]
  S4 = Pushbutton [package="[THT]"]
  R1 = Resistor [tolerance=±5% power=0.25 resistance=220 package=THT]
  R2 = Resistor [tolerance=±5% power=0.25 resistance=220 package=THT]
  R3 = Resistor [tolerance=±5% power=0.25 resistance=220 package=THT]
  R4 = Resistor [tolerance=±5% power=0.25 resistance=220 package=THT]
  LED1 = LED - 3mm [color="Red (633nm)" current=0.030 package="3 mm [THT]"]
  LED2 = LED - 3mm [color="Green (555nm)" current=0.030 package="3 mm [THT]"]
  LED3 = LED - 3mm [color="Blue (470nm)" current=0.030 package="3 mm [THT]"]
  LED4 = LED - 3mm [color="Yellow (595nm)" current=0.030 package="3 mm [THT]"]
  R5 = Resistor [tolerance=±5% power=0.25 resistance=220 package=THT]
  R6 = Resistor [tolerance=±5% power=0.25 resistance=220 package=THT]
  R7 = Resistor [tolerance=±5% power=0.25 resistance=220 package=THT]
  R8 = Resistor [tolerance=±5% power=0.25 resistance=220 package=THT]
  J1 = Piezo Speaker

nets:
  N1: WeMos_D1_Mini1.5V, S1.Pin_3, S1.Pin_4, S2.Pin_3, S2.Pin_4, S3.Pin_3, S3.Pin_4, S4.Pin_3, S4.Pin_4
  N2: WeMos_D1_Mini1.G, R1.Pin_0, R2.Pin_0, R3.Pin_0, R4.Pin_0, R5.Pin_1, R6.Pin_1, R7.Pin_1, R8.Pin_1, J1.pin1
  N3: S1.Pin_1, S1.Pin_2, R4.Pin_1
  N4: S2.Pin_1, S2.Pin_2, R2.Pin_1
  N5: S3.Pin_1, S3.Pin_2, R3.Pin_1
  N6: S4.Pin_1, S4.Pin_2, R1.Pin_1
  N7: LED1.cathode, R5.Pin_0
  N8: LED2.cathode, R6.Pin_0
  N9: LED3.cathode, R7.Pin_0
  N10: LED4.cathode, R8.Pin_0
