# Fritzing sketch simon_nodemcu_32s (saved by Fritzing 0.9.9b)
breadboards: 1

parts:
  S1 = Pushbutton [package="[THT]"]
  S2 = Pushbutton [package="[THT]"]
  S3 = Pushbutton [package="[THT]"]
  S4 = Pushbutton [package="[THT]"]
  R1 = Resistor [tolerance=±5% power=0.25 resistance=220 package=THT]
  R2 = Resistor [tolerance=±5% power=0.25 resistance=220 package=THT]
  R3 = Resistor [tolerance=±5% power=0.25 resistance=220 package=THT]
  R4 = Resistor [tolerance=±5% power=0.25 resistance=220 package=THT]
  LED1 = LED - 3mm [color="Red (633nm)" current=0.030 package="3 mm [THT]"]
  LED2 = LED - 3mm [color="Green (555nm)" current=0.030 package="3 mm [THT]"]
  LED3 = LED - 3mm [color="Blue (470nm)" current=0.030 package="3 mm [THT]"]
  LED4 = LED - 3mm [color="Yellow (595nm)" current=0.030 package="3 mm [THT]"]
  R5 = Resistor [tolerance=±5% power=0.25 resistance=220 package=THT]
  R6 = Resistor [tolerance=±5% power=0.25 resistance=220 package=THT]
  R7 = Resistor [tolerance=±5% power=0.25 resistance=220 package=THT]
  R8 = Resistor [tolerance=±5% power=0.25 resistance=220 package=THT]
  J1 = Piezo Speaker
  U1 = NodeMCU V1.0

nets:
  N1: S1.Pin_1, S1.Pin_2, R4.Pin_0, U1.D1
  N2: S1.Pin_3, S1.Pin_4, S2.Pin_3, S2.Pin_4, S3.Pin_3, S3.Pin_4, S4.Pin_3, S4.Pin_4, U1.D2, U1.Vin
  N3: S2.Pin_1, S2.Pin_2, R2.Pin_0
  N4: S3.Pin_1, S3.Pin_2, R3.Pin_0, U1.D3
  N5: S4.Pin_1, S4.Pin_2, R1.Pin_0, U1.D4
  N6: R1.Pin_1, R2.Pin_1, R3.Pin_1, R4.Pin_1, R5.Pin_1, R6.Pin_1, R7.Pin_1, R8.Pin_1, J1.pin1, U1.GND
  N7: LED1.cathode, R5.Pin_0
  N8: LED1.anode, U1.D0
  N9: LED2.cathode, R6.Pin_0
  N10: LED2.anode, U1.D5
  N11: LED3.cathode, R7.Pin_0
  N12: LED3.anode, U1.D6
  N13: LED4.cathode, R8.Pin_0
  N14: LED4.anode, U1.D7
  N15: J1.pin2, U1.D8

custom parts:
  NodeMCU V1.0: ESP8266 based NodeMCU
